// Logisim project ALU.circ as structural Verilog: 15 circuits, main circuit LeftShift32
module LeftShift32 (
  input  [31:0] B,
  input  Cin,
  input  [4:0] Sa,
  output [31:0] C
);

  wire [31:0] leftshift1_1_cout, leftshift2_1_cout, leftshift4_1_cout, leftshift8_1_cout, leftshift16_1_cout,
       multiplexer_1_out, multiplexer_2_out, multiplexer_3_out, multiplexer_4_out;

  Multiplexer #(.width(32), .enable("false")) multiplexer_1 (
    .in0(B), .in1(leftshift1_1_cout), .out(multiplexer_1_out), .sel(Sa[0]));
  LeftShift1 leftshift1_1 (.Cin(Cin), .A(B), .Cout(leftshift1_1_cout));
  Multiplexer #(.width(32), .enable("false")) multiplexer_2 (
    .in0(multiplexer_1_out), .in1(leftshift2_1_cout), .out(multiplexer_2_out), .sel(Sa[1]));
  LeftShift2 leftshift2_1 (.Cin(Cin), .A(multiplexer_1_out), .Cout(leftshift2_1_cout));
  LeftShift4 leftshift4_1 (.Cin(Cin), .A(multiplexer_2_out), .Cout(leftshift4_1_cout));
  Multiplexer #(.width(32), .enable("false")) multiplexer_3 (
    .in0(multiplexer_2_out), .in1(leftshift4_1_cout), .out(multiplexer_3_out), .sel(Sa[2]));
  LeftShift8 leftshift8_1 (.Cin(Cin), .A(multiplexer_3_out), .Cout(leftshift8_1_cout));
  Multiplexer #(.width(32), .enable("false")) multiplexer_4 (
    .in0(multiplexer_3_out), .in1(leftshift8_1_cout), .out(multiplexer_4_out), .sel(Sa[3]));
  LeftShift16 leftshift16_1 (.Cin(Cin), .A(multiplexer_4_out), .Cout(leftshift16_1_cout));
  Multiplexer #(.width(32), .enable("false")) multiplexer_5 (
    .in0(multiplexer_4_out), .in1(leftshift16_1_cout), .out(C), .sel(Sa[4]));
endmodule

module Add32 (
  input  Cin,
  input  [31:0] A,
  input  [31:0] B,
  output [31:0] C,
  output V
);

  wire add16_1_cout;

  Add16 add16_1 (.Cin(Cin), .Sub(Cin), .A(A[15:0]), .B(B[15:0]), .S(C[15:0]), .Cout(add16_1_cout));  // open: V
  Add16 add16_2 (.Cin(add16_1_cout), .Sub(Cin), .A(A[31:16]), .B(B[31:16]), .S(C[31:16]), .V(V));  // open: Cout
endmodule

module ALU32 (
  input  [31:0] A,
  input  [31:0] B,
  input  [3:0] Op,
  input  [4:0] Sa,
  output V,
  output [31:0] C
);

  wire add32_1_v, EV;
  wire [31:0] add32_1_c, and_2_out, le_1_cout, lrshift32_1_s, multiplexer_1_out, multiplexer_2_out,
       ne_1_cout, nor_1_out, or_1_out, xor_1_out;

  and and_1 (EV, Op[1], ~Op[3]);  // AND_Gate
  assign and_2_out = A & B;  // AND_Gate and_2, 32 bits wide
  assign or_1_out = A | B;  // OR_Gate or_1, 32 bits wide
  assign xor_1_out = A ^ B;  // XOR_Gate xor_1, 32 bits wide
  assign nor_1_out = ~(A | B);  // NOR_Gate nor_1, 32 bits wide
  Add32 add32_1 (.Cin(Op[2]), .A(A), .B(B), .C(add32_1_c), .V(add32_1_v));
  LRShift32 lrshift32_1 (.A(B), .Opcode({Op[3], Op[0]}), .Sa(Sa), .S(lrshift32_1_s));
  and and_3 (V, add32_1_v, EV);
  Multiplexer #(.width(32), .enable("false")) multiplexer_1 (
    .in0(and_2_out), .in1(or_1_out), .out(multiplexer_1_out), .sel(Op[0]));
  Multiplexer #(.width(32), .enable("false")) multiplexer_2 (
    .in0(xor_1_out), .in1(nor_1_out), .out(multiplexer_2_out), .sel(Op[0]));
  ne ne_1 (.A(xor_1_out), .eq(Op[0]), .Cout(ne_1_cout));
  le le_1 (.A(A), .gt(Op[0]), .Cout(le_1_cout));
  Multiplexer #(.select(3), .width(32), .enable("false")) multiplexer_3 (
    .in0(lrshift32_1_s), .in1(add32_1_c), .in2(multiplexer_1_out), .in3(add32_1_c), .in4(ne_1_cout),
    .in5(multiplexer_2_out), .in6(lrshift32_1_s), .in7(le_1_cout), .out(C), .sel(Op[3:1]));

  // Notes on the sheet:
  //   Split 4bit opcode to get 3 rightmost bits to send to Mux
  //   The leftmost bit determines subfunction
  //   LRShift
  //   Add/Sub Cin
  //   EV checks if V can be outputted
  //   LRShift32 has its own governing 2bit opcode
  //   eq, gt signals change the default behavior
  //   Mux groups:
  //   001x: add
  //   011x: sub
  //   000x: SLL
  //   010x: AND(0), OR(1)
  //   100x: ne(0), eq(1)
  //   101x: XOR(0), NOR(1)
  //   110x: SRL(0), SRA(1)
  //   111x: le(0), gt(1)
  //   In a group with 2 functions, x is defined by the bit in parentheses (x) respectively
endmodule

module Add1 (
  input  A,
  input  B,
  input  Cin,
  output S,
  output Cout
);

  wire and_1_out, and_2_out, xor_1_out;

  xor xor_1 (xor_1_out, A, B);
  and and_1 (and_1_out, xor_1_out, Cin);
  and and_2 (and_2_out, A, B);
  xor xor_2 (S, xor_1_out, Cin);
  or or_1 (Cout, and_1_out, and_2_out);
endmodule

module Add4 (
  input  Cin,
  input  [3:0] A,
  input  [3:0] B,
  input  Sub,
  output [3:0] S,
  output Cout,
  output V
);

  wire add1_1_cout, add1_2_cout, add1_3_cout, xor_1_out, xor_2_out, xor_3_out, xor_4_out;

  xor xor_1 (xor_1_out, B[0], Sub);
  Add1 add1_1 (.A(A[0]), .B(xor_1_out), .Cin(Cin), .S(S[0]), .Cout(add1_1_cout));
  xor xor_2 (xor_2_out, B[1], Sub);
  Add1 add1_2 (.A(A[1]), .B(xor_2_out), .Cin(add1_1_cout), .S(S[1]), .Cout(add1_2_cout));
  xor xor_3 (xor_3_out, B[2], Sub);
  Add1 add1_3 (.A(A[2]), .B(xor_3_out), .Cin(add1_2_cout), .S(S[2]), .Cout(add1_3_cout));
  xor xor_4 (xor_4_out, B[3], Sub);
  Add1 add1_4 (.A(A[3]), .B(xor_4_out), .Cin(add1_3_cout), .S(S[3]), .Cout(Cout));
  xor xor_5 (V, Cout, add1_3_cout);
endmodule

module Add16 (
  input  Cin,
  input  Sub,
  input  [15:0] A,
  input  [15:0] B,
  output [15:0] S,
  output Cout,
  output V
);

  wire add4_1_cout, add4_2_cout, add4_3_cout;

  Add4 add4_1 (.Cin(Cin), .A(A[3:0]), .B(B[3:0]), .Sub(Sub), .S(S[3:0]), .Cout(add4_1_cout));  // open: V
  Add4 add4_2 (.Cin(add4_1_cout), .A(A[7:4]), .B(B[7:4]), .Sub(Sub), .S(S[7:4]), .Cout(add4_2_cout));  // open: V
  Add4 add4_3 (.Cin(add4_2_cout), .A(A[11:8]), .B(B[11:8]), .Sub(Sub), .S(S[11:8]), .Cout(add4_3_cout));  // open: V
  Add4 add4_4 (.Cin(add4_3_cout), .A(A[15:12]), .B(B[15:12]), .Sub(Sub), .S(S[15:12]), .Cout(Cout), .V(V));
endmodule

module ne (
  input  [31:0] A,
  input  eq,
  output [31:0] Cout
);

  wire or_1_out, xor_1_out;

  or or_1 (or_1_out, A[0], A[1], A[2], A[3], A[4], A[5], A[6], A[7], A[8], A[9], A[10], A[11], A[12], A[13], A[14], A[15], A[17], A[18], A[19], A[20], A[21], A[22], A[23], A[24], A[25], A[26], A[27], A[28], A[29], A[30], A[31], A[16]);
  xor xor_1 (xor_1_out, or_1_out, eq);
  assign Cout = {{31{1'b0}}, xor_1_out};  // Bit_Extender bit_extender_1
endmodule

module le (
  input  [31:0] A,
  input  gt,
  output [31:0] Cout
);

  wire not_1_out, or_1_out, or_2_out, xor_1_out;

  or or_1 (or_1_out, A[0], A[1], A[2], A[3], A[4], A[5], A[6], A[7], A[8], A[9], A[10], A[11], A[12], A[13], A[14], A[15], A[17], A[18], A[19], A[20], A[21], A[22], A[23], A[24], A[25], A[26], A[27], A[28], A[29], A[30], A[31], A[16]);
  not not_1 (not_1_out, or_1_out);
  or or_2 (or_2_out, not_1_out, A[31]);
  xor xor_1 (xor_1_out, or_2_out, gt);
  assign Cout = {{31{1'b0}}, xor_1_out};  // Bit_Extender bit_extender_1
endmodule

module LeftShift1 (
  input  Cin,
  input  [31:0] A,
  output [31:0] Cout
);


  assign Cout = {A[30:0], Cin};

  // Notes on the sheet:
  //   Shift Left
endmodule

module LeftShift2 (
  input  Cin,
  input  [31:0] A,
  output [31:0] Cout
);

  wire [31:0] leftshift1_1_cout;

  LeftShift1 leftshift1_1 (.Cin(Cin), .A(A), .Cout(leftshift1_1_cout));
  LeftShift1 leftshift1_2 (.Cin(Cin), .A(leftshift1_1_cout), .Cout(Cout));

  // Notes on the sheet:
  //   Left Shift 2
endmodule

module LeftShift4 (
  input  Cin,
  input  [31:0] A,
  output [31:0] Cout
);

  wire [31:0] leftshift2_1_cout;

  LeftShift2 leftshift2_1 (.Cin(Cin), .A(A), .Cout(leftshift2_1_cout));
  LeftShift2 leftshift2_2 (.Cin(Cin), .A(leftshift2_1_cout), .Cout(Cout));

  // Notes on the sheet:
  //   Left Shift 4
endmodule

module LeftShift8 (
  input  Cin,
  input  [31:0] A,
  output [31:0] Cout
);

  wire [31:0] leftshift4_1_cout;

  LeftShift4 leftshift4_1 (.Cin(Cin), .A(A), .Cout(leftshift4_1_cout));
  LeftShift4 leftshift4_2 (.Cin(Cin), .A(leftshift4_1_cout), .Cout(Cout));

  // Notes on the sheet:
  //   Left Shift 8
endmodule

module LeftShift16 (
  input  Cin,
  input  [31:0] A,
  output [31:0] Cout
);

  wire [31:0] leftshift8_1_cout;

  LeftShift8 leftshift8_1 (.Cin(Cin), .A(A), .Cout(leftshift8_1_cout));
  LeftShift8 leftshift8_2 (.Cin(Cin), .A(leftshift8_1_cout), .Cout(Cout));

  // Notes on the sheet:
  //   Left Shift 16
endmodule

module reverse (
  input  [31:0] A,
  output [31:0] B,
  output Sign
);


  assign B = {A[0], A[1], A[2], A[3], A[4], A[5], A[6], A[7], A[8], A[9], A[10], A[11], A[12], A[13], A[14], A[15], A[16], A[17], A[18], A[19], A[20], A[21], A[22], A[23], A[24], A[25], A[26], A[27], A[28], A[29], A[30], A[31]};
  assign Sign = A[31];
endmodule

module LRShift32 (
  input  [31:0] A,
  input  [1:0] Opcode,
  input  [4:0] Sa,
  output [31:0] S
);

  wire and_1_out, reverse_1_sign;
  wire [31:0] leftshift32_1_c, multiplexer_1_out, reverse_1_b, reverse_2_b;

  reverse reverse_1 (.A(A), .B(reverse_1_b), .Sign(reverse_1_sign));
  Multiplexer #(.width(32), .enable("false")) multiplexer_1 (
    .in0(A), .in1(reverse_1_b), .out(multiplexer_1_out), .sel(Opcode[1]));
  and and_1 (and_1_out, reverse_1_sign, Opcode[0], Opcode[1]);
  LeftShift32 leftshift32_1 (.B(multiplexer_1_out), .Cin(and_1_out), .Sa(Sa), .C(leftshift32_1_c));
  reverse reverse_2 (.A(leftshift32_1_c), .B(reverse_2_b));  // open: Sign
  Multiplexer #(.width(32), .enable("false")) multiplexer_2 (
    .in0(leftshift32_1_c), .in1(reverse_2_b), .out(S), .sel(Opcode[1]));
endmodule
